// Logisim project regfile.circ as structural Verilog: 1 circuit, main circuit main
module main (
  input  [31:0] in_1,
  input  [4:0] rs1,
  input  [4:0] rs2,
  input  [4:0] rd,
  input  [31:0] Write_Data,
  input  RegWEn,
  output [31:0] ra,
  output [31:0] sp,
  output [31:0] t0,
  output [31:0] t1,
  output [31:0] t2,
  output [31:0] s0,
  output [31:0] s1,
  output [31:0] a0,
  output [31:0] Read_Data_1,
  output [31:0] Read_Data_2
);

  wire and_1_out, and_2_out, and_3_out, and_4_out, and_5_out, and_6_out, and_7_out, and_8_out, clk,
       comparator_1_eq, comparator_2_eq, comparator_3_eq, comparator_4_eq, comparator_5_eq, comparator_6_eq,
       comparator_7_eq, comparator_8_eq;
  wire [31:0] zero;

  Multiplexer #(.select(5), .width(32), .enable("false")) multiplexer_1 (
    .in0(zero), .in1(ra), .in2(sp), .in5(t0), .in6(t1), .in7(t2), .in8(s0), .in9(s1), .in10(a0),
    .out(Read_Data_1), .sel(rs1));  // open: in3, in4, in11, in12, in13, in14, in15, in16, in17, in18, in19, in20, in21, in22, in23, in24, in25, in26, in27, in28, in29, in30, in31
  Clock clock_1 (.out(clk));
  Multiplexer #(.select(5), .width(32), .enable("false")) multiplexer_2 (
    .in0(zero), .in1(ra), .in2(sp), .in5(t0), .in6(t1), .in7(t2), .in8(s0), .in9(s1), .in10(a0),
    .out(Read_Data_2), .sel(rs2));  // open: in3, in4, in11, in12, in13, in14, in15, in16, in17, in18, in19, in20, in21, in22, in23, in24, in25, in26, in27, in28, in29, in30, in31
  Register #(.width(32)) register_1 (.D(in_1), .clk(clk), .Q(zero));  // open: en, clr
  Comparator #(.width(5), .mode("unsigned")) comparator_1 (.a(5'b00001), .b(rd), .eq(comparator_1_eq));  // open: gt, lt
  Comparator #(.width(5), .mode("unsigned")) comparator_2 (.a(5'b00101), .b(rd), .eq(comparator_2_eq));  // open: gt, lt
  Comparator #(.width(5), .mode("unsigned")) comparator_3 (.a(5'b00111), .b(rd), .eq(comparator_3_eq));  // open: gt, lt
  Comparator #(.width(5), .mode("unsigned")) comparator_4 (.a(5'b01001), .b(rd), .eq(comparator_4_eq));  // open: gt, lt
  Register #(.width(32)) register_2 (.D(Write_Data), .en(and_1_out), .clk(clk), .Q(ra));  // open: clr
  and and_1 (and_1_out, comparator_1_eq, RegWEn);
  Register #(.width(32)) register_3 (.D(Write_Data), .en(and_2_out), .clk(clk), .Q(t0));  // open: clr
  and and_2 (and_2_out, comparator_2_eq, RegWEn);
  and and_3 (and_3_out, comparator_3_eq, RegWEn);
  and and_4 (and_4_out, comparator_4_eq, RegWEn);
  Register #(.width(32)) register_4 (.D(Write_Data), .en(and_3_out), .clk(clk), .Q(t2));  // open: clr
  Register #(.width(32)) register_5 (.D(Write_Data), .en(and_4_out), .clk(clk), .Q(s1));  // open: clr
  Comparator #(.width(5), .mode("unsigned")) comparator_5 (.a(5'b00110), .b(rd), .eq(comparator_5_eq));  // open: gt, lt
  Comparator #(.width(5), .mode("unsigned")) comparator_6 (.a(5'b01000), .b(rd), .eq(comparator_6_eq));  // open: gt, lt
  Comparator #(.width(5), .mode("unsigned")) comparator_7 (.a(5'b00010), .b(rd), .eq(comparator_7_eq));  // open: gt, lt
  and and_5 (and_5_out, comparator_5_eq, RegWEn);
  and and_6 (and_6_out, comparator_6_eq, RegWEn);
  Comparator #(.width(5), .mode("unsigned")) comparator_8 (.a(5'b01010), .b(rd), .eq(comparator_8_eq));  // open: gt, lt
  Register #(.width(32)) register_6 (.D(Write_Data), .en(and_7_out), .clk(clk), .Q(sp));  // open: clr
  and and_7 (and_7_out, comparator_7_eq, RegWEn);
  Register #(.width(32)) register_7 (.D(Write_Data), .en(and_5_out), .clk(clk), .Q(t1));  // open: clr
  Register #(.width(32)) register_8 (.D(Write_Data), .en(and_6_out), .clk(clk), .Q(s0));  // open: clr
  Register #(.width(32)) register_9 (.D(Write_Data), .en(and_8_out), .clk(clk), .Q(a0));  // open: clr
  and and_8 (and_8_out, comparator_8_eq, RegWEn);

  // Other names for the same wires on the sheet: read_data1[31:0] = Read_Data_1; read_data2[31:0] = Read_Data_2;
  //   read_reg1[4:0] = rs1; read_reg2[4:0] = rs2; write_en = RegWEn; write_reg[4:0] = rd

  // Notes on the sheet:
  //   INPUTS to your circuit
  //   DON'T CHANGE THE LOCATIONS OF THE INPUTS AND OUTPUTS!
  //   These are DEBUG/TEST outputs from your circuit.
  //   OUTPUTS from your circuit
endmodule
